# Fritzing sketch Esquema conexiones sin accesorios (saved by Fritzing 1.0.1rc)
breadboards: 1

parts:
  BAT1 = LIPO-110mAh [package=lipo-110]
  Part3 = Arduino Nano (Rev3.0)
  S2 = Pololu QTR-8 Reflectabce Sensor array [package=THT]
  Part4 = Motor Driver 1A Dual TB6612FNG  # not connected
  M3 = DC Mini Metal Gear Motor  # not connected
  M4 = DC Mini Metal Gear Motor  # not connected

nets:
  N1: BAT1.-, Part3.GND, S2.pin1, S2.pin15
  N2: Part3.5V, S2.pin14
  N3: Part3.A7, S2.pin5
  N4: Part3.A6, S2.pin6
  N5: Part3.A5, S2.pin7
  N6: Part3.A4, S2.pin8
  N7: Part3.A3, S2.pin9
  N8: Part3.A2, S2.pin10
  N9: Part3.A1, S2.pin11
  N10: Part3.A0, S2.pin12
