# Fritzing sketch Esquema conexiones (saved by Fritzing 1.0.1rc)
perfboards: 1

parts:
  Part1 = Arduino Nano (Rev3.0)
  S1 = Pololu QTR-8 Reflectabce Sensor array [package=THT]
  Part2 = Motor Driver 1A Dual TB6612FNG
  BAT1 = LIPO-110mAh [package=lipo-110]

nets:
  GND: Part1.GND, Part1.A7, Part1.A6, Part1.A5, Part1.A4, Part1.A3, Part1.A2, S1.pin1, S1.pin3, S1.pin5, S1.pin6, S1.pin7, S1.pin8, S1.pin9, S1.pin10, S1.pin15, S1.pin16, S1.pin17, S1.pin18, S1.pin19, S1.pin20, S1.pin21, Part2.GND
  N1: Part1.D4, Part2.STBY
  N2: Part1.D5, Part2.PWMA
  N3: Part1.D6, Part2.PWMB
  N4: Part1.D7, Part2.AIN2
  N5: Part1.D8, Part2.AIN1
  N6: Part1.D9, Part2.BIN1
  N7: Part1.D10, Part2.BIN2
  N8: Part1.VIN, BAT1.+
  N9: Part1.5V, Part1.A1, S1.pin11, S1.pin14, S1.pin22
  N10: Part1.A0, Part1.D13/SCK, S1.pin12, S1.pin13, S1.pin23
